// Logisim project newcpu.circ as structural Verilog: 3 circuits, main circuit main
module main (
  input  in_1,
  input  [7:0] in_2,
  input  in_3
);

  wire clock_1_out, d1, d2, d3, d4;
  wire [3:0] s1h, s1l, s2h, s2l, s3h, s3l, s4h, s4l;
  wire [7:0] segdisplay_1_hseg;

  Clock clock_1 (.out(clock_1_out));
  _7_Segment_Display digit4 (
    .g(s4h[3]), .f(s4h[2]), .a(s4h[1]), .b(s4h[0]), .e(s4l[3]), .d(s4l[2]), .c(s4l[1]), .dp(s4l[0]));
  _7_Segment_Display digit3 (
    .g(s3h[3]), .f(s3h[2]), .a(s3h[1]), .b(s3h[0]), .e(s3l[3]), .d(s3l[2]), .c(s3l[1]), .dp(s3l[0]));
  _7_Segment_Display digit2 (
    .g(s2h[3]), .f(s2h[2]), .a(s2h[1]), .b(s2h[0]), .e(s2l[3]), .d(s2l[2]), .c(s2l[1]), .dp(s2l[0]));
  _7_Segment_Display digit1 (
    .g(s1h[3]), .f(s1h[2]), .a(s1h[1]), .b(s1h[0]), .e(s1l[3]), .d(s1l[2]), .c(s1l[1]), .dp(s1l[0]));
  segdisplay segdisplay_1 (
    .reset(in_1), .clk(clock_1_out), .value(in_2), .en(in_3), .anode({d4, d3, d2, d1}),
    .hseg(segdisplay_1_hseg));  // open: sign
  assign {s1h, s1l} = d1 ? segdisplay_1_hseg : 8'bz;  // Controlled_Buffer controlled_buffer_1
  assign {s2h, s2l} = d2 ? segdisplay_1_hseg : 8'bz;  // Controlled_Buffer controlled_buffer_2
  assign {s3h, s3l} = d3 ? segdisplay_1_hseg : 8'bz;  // Controlled_Buffer controlled_buffer_3
  assign {s4h, s4l} = d4 ? segdisplay_1_hseg : 8'bz;  // Controlled_Buffer controlled_buffer_4
endmodule

module ring (
  input  clr,
  input  clk,
  output [3:0] Q
);

  wire q4, q5, q6, q7;

  D_Flip_Flop d_ff_1 (.D(q6), .clk(clk), .Q(q7), .reset(clr));  // open: Qn, preset
  D_Flip_Flop d_ff_2 (.D(q5), .clk(clk), .Q(q6), .reset(clr));  // open: Qn, preset
  D_Flip_Flop d_ff_3 (.D(q4), .clk(clk), .Q(q5), .reset(clr));  // open: Qn, preset
  D_Flip_Flop d_ff_4 (.D(Q[3]), .clk(clk), .Q(q4), .reset(clr));  // open: Qn, preset
  D_Flip_Flop d_ff_5 (.D(Q[2]), .clk(clk), .Q(Q[3]), .reset(clr));  // open: Qn, preset
  D_Flip_Flop d_ff_6 (.D(Q[1]), .clk(clk), .Q(Q[2]), .reset(clr));  // open: Qn, preset
  D_Flip_Flop d_ff_7 (.D(Q[0]), .clk(clk), .Q(Q[1]), .reset(clr));  // open: Qn, preset
  D_Flip_Flop d_ff_8 (.D(Q[3]), .clk(clk), .Q(Q[0]), .preset(clr));  // open: Qn, reset
endmodule

module segdisplay (
  input  reset,
  input  clk,
  input  [7:0] value,
  input  sign,
  input  en,
  output [3:0] anode,
  output [7:0] hseg
);

  wire [3:0] ring_1_p3;
  wire [7:0] SEGROM_data;

  ROM #(.addrWidth(13)) SEGROM (.addr({1'b0, ring_1_p3, value}), .data(SEGROM_data));
  // ring ring_1: pin names not known; wires that end beside it: reset, clk, ring_1_p3
  assign anode = en ? ring_1_p3 : 4'bz;  // Controlled_Buffer controlled_buffer_1
  assign hseg = en ? SEGROM_data : 8'bz;  // Controlled_Buffer controlled_buffer_2

  // Other names for the same wires on the sheet: clr = reset; sgn = sign

  // Notes on the sheet:
  //   contents of SEGROM (hex, n*v repeats v):
  //   256*0 7e 12 bc b6 d2 e6 ee 32 fe f2 7e 12 bc b6 d2 e6 ee 32 fe f2 7e 12 bc b6 d2 e6 ee 32 fe f2 7e
  //   12 bc b6 d2 e6 ee 32 fe f2 7e 12 bc b6 d2 e6 ee 32 fe f2 7e 12 bc b6 d2 e6 ee 32 fe f2 7e 12 bc b6
  //   d2 e6 ee 32 fe f2 7e 12 bc b6 d2 e6 ee 32 fe f2 7e 12 bc b6 d2 e6 ee 32 fe f2 7e 12 bc b6 d2 e6 ee
  //   32 fe f2 7e 12 bc b6 d2 e6 ee 32 fe f2 7e 12 bc b6 d2 e6 ee 32 fe f2 7e 12 bc b6 d2 e6 ee 32 fe f2
  //   7e 12 bc b6 d2 e6 ee 32 fe f2 7e 12 bc b6 d2 e6 ee 32 fe f2 7e 12 bc b6 d2 e6 ee 32 fe f2 7e 12 bc
  //   b6 d2 e6 ee 32 fe f2 7e 12 bc b6 d2 e6 ee 32 fe f2 7e 12 bc b6 d2 e6 ee 32 fe f2 7e 12 bc b6 d2 e6
  //   ee 32 fe f2 7e 12 bc b6 d2 e6 ee 32 fe f2 7e 12 bc b6 d2 e6 ee 32 fe f2 7e 12 bc b6 d2 e6 ee 32 fe
  //   f2 7e 12 bc b6 d2 e6 ee 32 fe f2 7e 12 bc b6 d2 e6 ee 32 fe f2 7e 12 bc b6 d2 e6 10*0 10*12 10*bc
  //   10*b6 10*d2 10*e6 10*ee 10*32 10*fe 10*f2 10*7e 10*12 10*bc 10*b6 10*d2 10*e6 10*ee 10*32 10*fe
  //   10*f2 10*7e 10*12 10*bc 10*b6 10*d2 6*e6 6*1 10*ff 340*0 100*12 56*bc
endmodule
